# Fritzing sketch montagemFritizing-ESP32s3 (saved by Fritzing 1.0.4)

parts:
  M1 = ESP32-S3-DevKitC-1-N8R8-v1 [part_number=ESP32-S3-DevKitC-1-N8R8-v1]
  LCD1 = TFT 3.5 inch 480x320 w touch and SD
  S1 = Pushbutton [package="[THT]"]
  R1 = Resistor [tolerance=±5% power=0.25W resistance=10000 package=THT]
  LED1 = LED - 5mm [color="Red (633nm)" current=0.030A package="5 mm [THT]"]
  R2 = Rotary Potentiometer (Small) [maximum_resistance=10kΩ knob_status=50% power=0.5W package=THT]
  R3 = Resistor [tolerance=±5% power=0.25W resistance=330 package=THT]

nets:
  N1: M1.pin_3, R1.Pin_0, R2.leg1
  N2: M1.pin_10, LCD1.Pin_11
  N3: M1.pin_11, LCD1.Pin_13
  N4: M1.pin_12, LCD1.Pin_5
  N5: M1.pin_15, LCD1.Pin_4
  N6: M1.pin_16, LCD1.Pin_3
  N7: M1.pin_17, LCD1.Pin_6
  N8: M1.pin_18, LCD1.Pin_7
  N9: M1.pin_19, LCD1.Pin_10
  N10: M1.pin_20, LCD1.Pin_12
  N11: M1.pin_21, LCD1.Pin_1, LCD1.Pin_8
  N12: M1.pin_23, M1.pin_24, M1.pin_44, LCD1.Pin_2, S1.Pin_2, LED1.cathode, R2.leg2
  N13: M1.pin_34, R2.wiper
  N14: M1.pin_35, R3.Pin_1
  N15: M1.pin_36, S1.Pin_3, S1.Pin_4, R1.Pin_1
  N16: LED1.anode, R3.Pin_0

custom parts:
  ESP32-S3-DevKitC-1-N8R8-v1: ESP32-S3-DevKitC-1-N8R8-v1 This module is 44pins long (2x22) and 11 pins width.
  TFT 3.5 inch 480x320 w touch and SD: This is a generic 1.8 tft spi lcd display available on ebay and others. The 1.8"3.5 inch 480X320 SPI TFT Module 320x480 LCD Display - Touch.
