# Fritzing sketch montagemFritizing-ESP32devkit (saved by Fritzing 1.0.4)
breadboards: 1

parts:
  LCD1 = TFT 3.5 inch 480x320 w touch and SD
  LED1 = LED - 5mm [color="Red (633nm)" current=0.030A package="5 mm [THT]"]
  R1 = Rotary Potentiometer (Small) [maximum_resistance=10kΩ knob_status=50% power=0.5W package=THT]
  esp2 = ESP32 DevKitc V4
  R2 = Resistor [tolerance=±5% power=0.25W resistance=10000 package=THT]
  S1 = Pushbutton [package="[THT]"]
  R3 = Resistor [tolerance=±5% power=0.25W resistance=330 package=THT]

nets:
  N1: LCD1.Pin_1, LCD1.Pin_8, esp2.5V
  N2: LCD1.Pin_2, LED1.cathode, R1.leg1, esp2.GND#18, S1.Pin_1, S1.Pin_2
  N3: LCD1.Pin_3, esp2.IO5
  N4: LCD1.Pin_4, esp2.IO4
  N5: LCD1.Pin_5, esp2.IO2
  N6: LCD1.Pin_6, esp2.IO23
  N7: LCD1.Pin_7, esp2.IO18
  N8: LCD1.Pin_11, esp2.IO21
  N9: LCD1.Pin_13, esp2.IO19
  N10: LED1.anode, R3.Pin_1
  N11: R1.wiper, esp2.IO17
  N12: R1.leg2, esp2.3V3, R2.Pin_0
  N13: esp2.IO16, R3.Pin_0
  N14: esp2.IO22, R2.Pin_1, S1.Pin_3, S1.Pin_4

custom parts:
  TFT 3.5 inch 480x320 w touch and SD: This is a generic 1.8 tft spi lcd display available on ebay and others. The 1.8"3.5 inch 480X320 SPI TFT Module 320x480 LCD Display - Touch.
  ESP32 DevKitc V4: ESP32-DevKitC board with ESP32-WROOM-32 module. ESP32-DevKitC V4 is a small-sized ESP32-based development board produced by Espressif. Most of the pins on the ESP module are broken out to the pin headers on the board. The pins D0, D1, D2, D3, CMD and CLK are used internally for communication between ESP32 and SPI flash memory. They are grouped on both sides near the USB connector. Avoid using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
